# Fritzing sketch Trombino (saved by Fritzing 0.8.5b)
stripboards: 2
breadboards: 1

parts:
  R1 = Resistor [tolerance=±5% resistance=10k package=THT]
  R2 = Resistor [tolerance=±5% resistance=10k package=THT]
  R3 = Resistor [tolerance=±5% resistance=10k package=THT]
  S1 = Pushbutton [package="[THT]"]
  S2 = Pushbutton [package="[THT]"]
  S3 = Pushbutton [package="[THT]"]
  Part1 = Arduino Uno (Rev3)
  LED1 = LED - 5mm [color="Red (633nm)" package="5 mm [THT]"]
  LED2 = LED - 5mm [color="Yellow (595nm)" package="5 mm [THT]"]
  LED3 = LED - 5mm [color="Green (570nm)" package="5 mm [THT]"]
  S4 = Pushbutton [package="[THT]"]
  TRS1 = Audio Jack (TRS) 3.5mm [package="PG203J [THT]"]
  R4 = Rotary Potentiometer (Small) [maximum_resistance=100kΩ package=THT]

nets:
  N1: R1.Pin_0, R2.Pin_0, R3.Pin_0, Part1.GND
  N2: R1.Pin_1, S1.Pin_3, S1.Pin_4, Part1.D4
  N3: R2.Pin_1, S3.Pin_3, S3.Pin_4, Part1.D2
  N4: R3.Pin_1, S2.Pin_3, S2.Pin_4, Part1.D3_PWM
  N5: S1.Pin_1, S1.Pin_2, S2.Pin_1, S2.Pin_2, S3.Pin_1, S3.Pin_2, Part1.5V
  N6: LED1.cathode, LED2.cathode, LED3.cathode, TRS1.Sleeve, R4.leg2
  N7: LED1.anode, S4.Pin_3, S4.Pin_4
  N8: S4.Pin_1, S4.Pin_2, R4.leg1
  N9: TRS1.Ring, TRS1.Tip
